# Fritzing sketch main_board_v0 (saved by Fritzing 0.9.3b)
circuit board: 22cm x 13.5cm
breadboards: 1

parts:
  U1_(PWR) = USB Connectors [package=usb-mb-h]
  U2_(USART1) = USB Connectors [package=usb-mb-h]
  I2C1_1 = male pin header, 4 pins [form="♂ (male)"]
  I2C1_2 = male pin header, 4 pins [form="♂ (male)"]
  I2C1_3 = male pin header, 4 pins [form="♂ (male)"]
  I2C1_4 = male pin header, 4 pins [form="♂ (male)"]
  CH340G_1 = SO16 [chip_label=IC package=SO]
  X1_12MHz = Crystal [frequency="1 MHz" package=THT]
  C1_22pF = Ceramic Capacitor [capacitance=22nF package="100 mil [THT, multilayer]"]
  C2_22pF = Ceramic Capacitor [capacitance=22nF package="100 mil [THT, multilayer]"]
  LED1 = smd LED [color="Green (565nm)" package="1206 [SMD]"]
  R1 = Resistor [tolerance=±5% resistance=1.5k package=THT]
  R2 = Resistor [tolerance=±5% resistance=1.5k package=THT]
  LED2 = smd LED [color="Yellow (585nm)" package="1206 [SMD]"]
  LED3 = smd LED [color="Yellow (585nm)" package="1206 [SMD]"]
  R3 = Resistor [tolerance=±5% resistance=1.5k package=THT]
  R4 = Resistor [tolerance=±5% resistance=1.5k package=THT]
  U3_(USART2) = USB Connectors [package=usb-mb-h]
  CH340G_2 = SO16 [chip_label=IC package=SO]
  X2_12MHz = Crystal [frequency="1 MHz" package=THT]
  C4_22pF = Ceramic Capacitor [capacitance=22nF package="100 mil [THT, multilayer]"]
  C5_22pF = Ceramic Capacitor [capacitance=22nF package="100 mil [THT, multilayer]"]
  C6_100nF = Ceramic Capacitor [capacitance=22nF package="100 mil [THT, multilayer]"]
  LED6 = smd LED [color="Yellow (585nm)" package="1206 [SMD]"]
  LED4 = smd LED [color="Green (565nm)" package="1206 [SMD]"]
  LED5 = smd LED [color="Yellow (585nm)" package="1206 [SMD]"]
  R5 = Resistor [tolerance=±5% resistance=1.5k package=THT]
  R6 = Resistor [tolerance=±5% resistance=1.5k package=THT]
  R7 = Resistor [tolerance=±5% resistance=1.5k package=THT]
  R8 = Resistor [tolerance=±5% resistance=1.5k package=THT]
  U4_(UART5) = USB Connectors [package=usb-mb-h]
  CH340G_3 = SO16 [chip_label=IC package=SO]
  X3_12MHz = Crystal [frequency="1 MHz" package=THT]
  C8_22pF = Ceramic Capacitor [capacitance=22nF package="100 mil [THT, multilayer]"]
  LED9 = smd LED [color="Yellow (585nm)" package="1206 [SMD]"]
  LED8 = smd LED [color="Yellow (585nm)" package="1206 [SMD]"]
  LED7 = smd LED [color="Green (565nm)" package="1206 [SMD]"]
  R10 = Resistor [tolerance=±5% resistance=1.5k package=THT]
  R11 = Resistor [tolerance=±5% resistance=1.5k package=THT]
  R12 = Resistor [tolerance=±5% resistance=1.5k package=THT]
  C3_100nF = Ceramic Capacitor [capacitance=22nF package="100 mil [THT, multilayer]"]
  PB_1 = male pin header, 8 pins [form="♂ (male)"]
  PA_1 = male pin header, 8 pins [form="♂ (male)"]
  MCP23017_2 = IC, DIP package, 28 pins [chip_label=IC]
  PB_2 = male pin header, 8 pins [form="♂ (male)"]
  PA_2 = male pin header, 8 pins [form="♂ (male)"]
  24LC256_1 = IC, DIP package, 8 pins [chip_label=IC]
  24LC256_2 = IC, DIP package, 8 pins [chip_label=IC]
  LM75 = IC, DIP package, 8 pins [chip_label=IC]
  WP_1 = female pin header, 3 pins [form="♀ (female)"]
  WP_2 = female pin header, 3 pins [form="♀ (female)"]
  DAC1_OUT = male pin header, 2 pins [form="♂ (male)"]
  LED0 = smd LED [color="Red (635nm)" package="1206 [SMD]"]
  R0 = Resistor [tolerance=±5% resistance=1.5k package=THT]
  PWR5V_1 = male pin header, 2 pins [form="♂ (male)"]
  PWR5V_2 = male pin header, 2 pins [form="♂ (male)"]
  PWR5V_3 = male pin header, 2 pins [form="♂ (male)"]
  PWR3V3_1 = male pin header, 2 pins [form="♂ (male)"]
  PWR3V3_2 = male pin header, 2 pins [form="♂ (male)"]
  PWR3V3_3 = male pin header, 2 pins [form="♂ (male)"]
  I2C2_4 = male pin header, 4 pins [form="♂ (male)"]
  I2C2_3 = male pin header, 4 pins [form="♂ (male)"]
  I2C2_2 = male pin header, 4 pins [form="♂ (male)"]
  I2C2_1 = male pin header, 4 pins [form="♂ (male)"]
  SPI2_1 = male pin header, 6 pins [form="♂ (male)"]
  SPI2_2 = male pin header, 6 pins [form="♂ (male)"]
  SPI2_3 = male pin header, 6 pins [form="♂ (male)"]
  USART1_RX_TX_GND = male pin header, 3 pins [form="♂ (male)"]
  USART2_RX_TX_GND = male pin header, 3 pins [form="♂ (male)"]
  DISPLAY = male pin header, 14 pins [form="♂ (male)"]
  PWM_1 = male pin header, 2 pins [form="♂ (male)"]
  PWM_2 = male pin header, 2 pins [form="♂ (male)"]
  PWM_3 = male pin header, 2 pins [form="♂ (male)"]
  ADC_1 = male pin header, 2 pins [form="♂ (male)"]
  ADC_3 = male pin header, 2 pins [form="♂ (male)"]
  ADC_2 = male pin header, 2 pins [form="♂ (male)"]
  EXTI_1 = male pin header, 2 pins [form="♂ (male)"]
  EXTI_2 = male pin header, 2 pins [form="♂ (male)"]
  EXTI_3 = male pin header, 2 pins [form="♂ (male)"]
  EXTI_4 = male pin header, 2 pins [form="♂ (male)"]
  EXTI_5 = male pin header, 2 pins [form="♂ (male)"]
  EXTI_6 = male pin header, 2 pins [form="♂ (male)"]
  EXTI_7 = male pin header, 2 pins [form="♂ (male)"]
  EXTI_8 = male pin header, 2 pins [form="♂ (male)"]
  ADC_4 = male pin header, 2 pins [form="♂ (male)"]
  PWM_4 = male pin header, 2 pins [form="♂ (male)"]
  LED12 = smd LED [color="Red (635nm)" package="1206 [SMD]"]
  R15 = Resistor [tolerance=±5% resistance=1.5k package=THT]
  LED11 = smd LED [color="Red (635nm)" package="1206 [SMD]"]
  LED10 = smd LED [color="Red (635nm)" package="1206 [SMD]"]
  R14 = Resistor [tolerance=±5% resistance=1.5k package=THT]
  R13 = Resistor [tolerance=±5% resistance=1.5k package=THT]
  Nucleo-F446RE = STM32 Nucleo boards
  MCP23017_1 = IC, DIP package, 28 pins [chip_label=IC]
  R9 = Resistor [tolerance=±5% resistance=1.5k package=THT]
  C9_100nF = Ceramic Capacitor [capacitance=22nF package="100 mil [THT, multilayer]"]
  C7_22pF = Ceramic Capacitor [capacitance=22nF package="100 mil [THT, multilayer]"]
  UART5_RX_TX_GND = male pin header, 3 pins [form="♂ (male)"]
  WeMos_D1_Mini1 = WeMos D1 Mini

nets:
  GND: U1_(PWR).GND, U2_(USART1).GND, I2C1_1.pin4, I2C1_2.pin4, I2C1_3.pin4, I2C1_4.pin4, CH340G_1.1, C1_22pF.0, C2_22pF.0, R1.Pin_1, U3_(USART2).GND, CH340G_2.1, C4_22pF.0, C5_22pF.0, C6_100nF.0, R5.Pin_1, U4_(UART5).GND, CH340G_3.1, C8_22pF.0, C3_100nF.0, MCP23017_2.pin10, 24LC256_1.pin1, 24LC256_1.pin2, 24LC256_1.pin3, 24LC256_1.pin4, 24LC256_2.pin2, 24LC256_2.pin3, 24LC256_2.pin4, LM75.pin4, LM75.pin5, LM75.pin6, LM75.pin7, WP_1.pin3, WP_2.pin3, DAC1_OUT.pin2, R0.Pin_1, PWR5V_1.pin2, PWR5V_2.pin2, PWR5V_3.pin2, PWR3V3_1.pin2, PWR3V3_2.pin2, PWR3V3_3.pin2, I2C2_4.pin4, I2C2_3.pin4, I2C2_2.pin4, I2C2_1.pin4, SPI2_1.pin6, SPI2_2.pin6, SPI2_3.pin6, USART1_RX_TX_GND.pin3, USART2_RX_TX_GND.pin3, DISPLAY.pin2, PWM_1.pin2, PWM_2.pin2, PWM_3.pin2, ADC_1.pin2, ADC_3.pin2, ADC_2.pin2, EXTI_1.pin2, EXTI_2.pin2, EXTI_3.pin2, EXTI_4.pin2, EXTI_5.pin2, EXTI_6.pin2, EXTI_7.pin2, EXTI_8.pin2, ADC_4.pin2, PWM_4.pin2, R15.Pin_1, R14.Pin_1, R13.Pin_1, Nucleo-F446RE.GND, MCP23017_1.pin10, MCP23017_1.pin15, R9.Pin_1, C9_100nF.0, C7_22pF.0, UART5_RX_TX_GND.pin3, WeMos_D1_Mini1.G
  5V: U1_(PWR).VBUS, LED0.anode, PWR5V_1.pin1, PWR5V_2.pin1, PWR5V_3.pin1, Nucleo-F446RE.E5V, WeMos_D1_Mini1.5V
  N1: U2_(USART1).D+, CH340G_1.5
  N2: U2_(USART1).D-, CH340G_1.6
  N3: U2_(USART1).VBUS, CH340G_1.4, CH340G_1.16, LED1.anode, R3.Pin_0, R4.Pin_0, C3_100nF.1
  I2C1_SCL: I2C1_1.pin1, I2C1_2.pin1, I2C1_3.pin1, I2C1_4.pin1, Nucleo-F446RE.PB6
  I2C1_SDA: I2C1_1.pin2, I2C1_2.pin2, I2C1_3.pin2, I2C1_4.pin2, Nucleo-F446RE.PB7
  M5V: I2C1_1.pin3, I2C1_2.pin3, I2C1_3.pin3, I2C1_4.pin3, MCP23017_2.pin9, MCP23017_2.pin15, MCP23017_2.pin16, MCP23017_2.pin17, MCP23017_2.pin18, 24LC256_1.pin8, 24LC256_2.pin1, 24LC256_2.pin8, LM75.pin8, WP_1.pin1, WP_2.pin1, I2C2_4.pin3, I2C2_3.pin3, I2C2_2.pin3, I2C2_1.pin3, SPI2_1.pin5, SPI2_2.pin5, SPI2_3.pin5, DISPLAY.pin1, DISPLAY.pin8, Nucleo-F446RE.5V, MCP23017_1.pin9, MCP23017_1.pin16, MCP23017_1.pin17, MCP23017_1.pin18
  N4: CH340G_1.2, R2.Pin_0, LED2.cathode
  USART1_TX: CH340G_1.3, LED3.cathode, USART1_RX_TX_GND.pin2, Nucleo-F446RE.PA9
  N5: CH340G_1.7, X1_12MHz.pin_0, C1_22pF.1
  N6: CH340G_1.8, X1_12MHz.pin_1, C2_22pF.1
  N7: LED1.cathode, R1.Pin_0
  USART1_RX: R2.Pin_1, USART1_RX_TX_GND.pin1, Nucleo-F446RE.PA10
  N8: LED2.anode, R3.Pin_1
  N9: LED3.anode, R4.Pin_1
  N10: U3_(USART2).D+, CH340G_2.5
  N11: U3_(USART2).D-, CH340G_2.6
  N12: U3_(USART2).VBUS, CH340G_2.4, CH340G_2.16, C6_100nF.1, LED4.anode, R7.Pin_0, R8.Pin_0
  N13: CH340G_2.2, LED5.cathode, R6.Pin_0
  USART2_TX: CH340G_2.3, LED6.cathode, USART2_RX_TX_GND.pin2, Nucleo-F446RE.PA2
  N14: CH340G_2.7, X2_12MHz.pin_0, C4_22pF.1
  N15: CH340G_2.8, X2_12MHz.pin_1, C5_22pF.1
  N16: LED6.anode, R8.Pin_1
  N17: LED4.cathode, R5.Pin_0
  N18: LED5.anode, R7.Pin_1
  USART2_RX: R6.Pin_1, USART2_RX_TX_GND.pin1, Nucleo-F446RE.PA3
  N19: U4_(UART5).D+, CH340G_3.5
  N20: U4_(UART5).D-, CH340G_3.6
  N21: U4_(UART5).VBUS, CH340G_3.4, CH340G_3.16, LED7.anode, R11.Pin_0, R12.Pin_0, C9_100nF.1
  N22: CH340G_3.2, LED8.cathode, R10.Pin_0
  UART5_TX: CH340G_3.3, LED9.cathode, Nucleo-F446RE.PC12, UART5_RX_TX_GND.pin2
  N23: CH340G_3.7, X3_12MHz.pin_0, C7_22pF.1
  N24: CH340G_3.8, X3_12MHz.pin_1, C8_22pF.1
  N25: LED9.anode, R12.Pin_1
  N26: LED8.anode, R11.Pin_1
  N27: LED7.cathode, R9.Pin_0
  UART5_RX: R10.Pin_1, Nucleo-F446RE.PD2, UART5_RX_TX_GND.pin1
  N28: PB_1.pin1, MCP23017_1.pin1
  N29: PB_1.pin2, MCP23017_1.pin2
  N30: PB_1.pin3, MCP23017_1.pin3
  N31: PB_1.pin4, MCP23017_1.pin4
  N32: PB_1.pin5, MCP23017_1.pin5
  N33: PB_1.pin6, MCP23017_1.pin6
  N34: PB_1.pin7, MCP23017_1.pin7
  N35: PB_1.pin8, MCP23017_1.pin8
  N36: PA_1.pin1, MCP23017_1.pin28
  N37: PA_1.pin2, MCP23017_1.pin27
  N38: PA_1.pin3, MCP23017_1.pin26
  N39: PA_1.pin4, MCP23017_1.pin25
  N40: PA_1.pin5, MCP23017_1.pin24
  N41: PA_1.pin6, MCP23017_1.pin23
  N42: PA_1.pin7, MCP23017_1.pin22
  N43: PA_1.pin8, MCP23017_1.pin21
  N44: MCP23017_2.pin1, PB_2.pin1
  N45: MCP23017_2.pin2, PB_2.pin2
  N46: MCP23017_2.pin3, PB_2.pin3
  N47: MCP23017_2.pin4, PB_2.pin4
  N48: MCP23017_2.pin5, PB_2.pin5
  N49: MCP23017_2.pin6, PB_2.pin6
  N50: MCP23017_2.pin7, PB_2.pin7
  N51: MCP23017_2.pin8, PB_2.pin8
  I2C2_SCL: MCP23017_2.pin12, 24LC256_1.pin6, 24LC256_2.pin6, LM75.pin2, I2C2_4.pin1, I2C2_3.pin1, I2C2_2.pin1, I2C2_1.pin1, Nucleo-F446RE.PB10, MCP23017_1.pin12
  I2C2_SDA: MCP23017_2.pin13, 24LC256_1.pin5, 24LC256_2.pin5, LM75.pin1, I2C2_4.pin2, I2C2_3.pin2, I2C2_2.pin2, I2C2_1.pin2, Nucleo-F446RE.PB11, MCP23017_1.pin13
  N52: MCP23017_2.pin21, PA_2.pin8
  N53: MCP23017_2.pin22, PA_2.pin7
  N54: MCP23017_2.pin23, PA_2.pin6
  N55: MCP23017_2.pin24, PA_2.pin5
  N56: MCP23017_2.pin25, PA_2.pin4
  N57: MCP23017_2.pin26, PA_2.pin3
  N58: MCP23017_2.pin27, PA_2.pin2
  N59: MCP23017_2.pin28, PA_2.pin1
  N60: 24LC256_1.pin7, WP_1.pin2
  N61: 24LC256_2.pin7, WP_2.pin2
  N62: DAC1_OUT.pin1, Nucleo-F446RE.PA4
  N63: LED0.cathode, R0.Pin_0
  M3V3: PWR3V3_1.pin1, PWR3V3_2.pin1, PWR3V3_3.pin1, Nucleo-F446RE.3v3
  SPI2_CS.1: SPI2_1.pin1, Nucleo-F446RE.PB0
  SPI2_SCK: SPI2_1.pin2, SPI2_2.pin2, SPI2_3.pin2, Nucleo-F446RE.PC7
  SPI2_MOSI: SPI2_1.pin3, SPI2_2.pin3, SPI2_3.pin3, Nucleo-F446RE.PC1
  SPI2_MISO: SPI2_1.pin4, SPI2_2.pin4, SPI2_3.pin4, Nucleo-F446RE.PC2
  SPI2_CS.2: SPI2_2.pin1, Nucleo-F446RE.PB1
  SPI2_CS.3: SPI2_3.pin1, Nucleo-F446RE.PB2
  SPI3_CS: DISPLAY.pin3, Nucleo-F446RE.PB13
  DISPL_RST: DISPLAY.pin4, Nucleo-F446RE.PB4
  DISPL_DC: DISPLAY.pin5, Nucleo-F446RE.PB15
  SPI3_MOSI: DISPLAY.pin6, DISPLAY.pin12, Nucleo-F446RE.PB5
  SPI3_SCK: DISPLAY.pin7, DISPLAY.pin10, Nucleo-F446RE.PC10
  SPI3_MISO: DISPLAY.pin9, DISPLAY.pin13, Nucleo-F446RE.PC11
  DISPL_TCS: DISPLAY.pin11, Nucleo-F446RE.PB8
  DISPL_TIRQ: DISPLAY.pin14, Nucleo-F446RE.PB9
  PWM1: PWM_1.pin1, Nucleo-F446RE.PB3
  PWM2: PWM_2.pin1, Nucleo-F446RE.PA8
  PWM3: PWM_3.pin1, Nucleo-F446RE.PA11
  ADC1: ADC_1.pin1, Nucleo-F446RE.PC0
  ADC3: ADC_3.pin1, Nucleo-F446RE.PC4
  ADC2: ADC_2.pin1, Nucleo-F446RE.PC3
  EXTI1: EXTI_1.pin1, Nucleo-F446RE.PA5
  EXTI2: EXTI_2.pin1, Nucleo-F446RE.PA6
  EXTI3: EXTI_3.pin1, Nucleo-F446RE.PA7
  EXTI4: EXTI_4.pin1, Nucleo-F446RE.PC8
  EXTI5: EXTI_5.pin1, Nucleo-F446RE.PA12
  EXTI6: EXTI_6.pin1, Nucleo-F446RE.PA13
  EXTI7: EXTI_7.pin1, Nucleo-F446RE.PA14
  EXTI8: EXTI_8.pin1, Nucleo-F446RE.PA15
  ADC4: ADC_4.pin1, Nucleo-F446RE.PC5
  PWM4: PWM_4.pin1, Nucleo-F446RE.PC6
  N64: LED12.cathode, R15.Pin_0
  N65: LED12.anode, WeMos_D1_Mini1.D7
  N66: LED11.cathode, R14.Pin_0
  N67: LED11.anode, WeMos_D1_Mini1.D6
  N68: LED10.cathode, R13.Pin_0
  N69: LED10.anode, WeMos_D1_Mini1.D5
  UART4_TX: Nucleo-F446RE.PA0, WeMos_D1_Mini1.RX
  UART4_RX: Nucleo-F446RE.PA1, WeMos_D1_Mini1.TX

notes:
  MAIN BOARD FOR GOS2022
  © Ahmed Ibrahim Gazar
  2024-03-13
  BOARD REVISION: A1
  5V
  GND
  SCL
  SDA
  VCC
